// Logisim project CPU_V2.circ as structural Verilog: 8 circuits, main circuit main
module main (
);

  wire alu, clk, data, dest, en, load, rom_1_1_alu_mux, rom_1_1_data_mux, rom_1_1_dest_mux, rom_1_1_en, rst;
  wire [3:0] I3t0I, I11t8I, I15t12I, multiplexer_1_out, multiplexer_3_out;
  wire [5:0] rom_1_1_settings, set;
  wire [7:0] alu_maison_1_output_alu, ALU_out, multiplexer_2_out, multiplexer_4_out, multiplexer_5_out,
       multiplexer_6_out, reg_file_1_l1, reg_file_1_l2, reg_file_2_l1, reg_file_2_l2;
  wire [7:4] I7t0I;
  wire [9:0] add_1_1_out_3, add_1_2_out_3, program_counter_1_out_4, program_counter_2_out_4;
  wire [15:0] inst_memory_1_output_code;

  Button button_1 (.out(rst));
  Button button_2 (.out(clk));
  Button button_3 (.out(load));
  add_1 add_1_1 (.INPUT_A(10'h1), .INPUT_B(program_counter_1_out_4), .out_3(add_1_1_out_3));
  Program_Counter program_counter_1 (.addr(add_1_1_out_3), .clk(clk), .rst(rst), .out_4(program_counter_1_out_4));
  add_1 add_1_2 (.INPUT_A(10'h1), .INPUT_B(program_counter_2_out_4), .out_3(add_1_2_out_3));
  Program_Counter program_counter_2 (.addr(add_1_2_out_3), .clk(clk), .rst(rst), .out_4(program_counter_2_out_4));
  inst_memory inst_memory_1 (
    .reset(rst), .load(load), .addr(program_counter_1_out_4), .output_code(inst_memory_1_output_code));
  inst_memory inst_memory_2 (
    .reset(rst), .load(load), .addr(program_counter_2_out_4), .output_code({I15t12I, I11t8I, I7t0I, I3t0I}));
  Multiplexer #(.width(4)) multiplexer_1 (
    .in0(inst_memory_1_output_code[3:0]), .in1(inst_memory_1_output_code[11:8]), .out(multiplexer_1_out),
    .sel(rom_1_1_dest_mux));
  Multiplexer #(.width(8)) multiplexer_2 (
    .in0(alu_maison_1_output_alu), .in1(inst_memory_1_output_code[7:0]), .out(multiplexer_2_out),
    .sel(rom_1_1_data_mux));
  ROM_1 rom_1_1 (
    .op_code(inst_memory_1_output_code[15:12]), .settings(rom_1_1_settings), .en(rom_1_1_en),
    .dest_MUX(rom_1_1_dest_mux), .data_MUX(rom_1_1_data_mux), .alu_MUX(rom_1_1_alu_mux));
  reg_file reg_file_1 (
    .Data(multiplexer_2_out), .en(rom_1_1_en), .clk(clk), .reset(rst), .W(multiplexer_1_out),
    .R1(inst_memory_1_output_code[11:8]), .R2(inst_memory_1_output_code[7:4]), .L1(reg_file_1_l1),
    .L2(reg_file_1_l2));
  Multiplexer #(.width(4)) multiplexer_3 (.in0(I3t0I), .in1(I11t8I), .out(multiplexer_3_out), .sel(dest));
  Multiplexer #(.width(8)) multiplexer_4 (.in0(ALU_out), .in1({I7t0I, I3t0I}), .out(multiplexer_4_out), .sel(data));
  ROM_1 rom_1_2 (.op_code(I15t12I), .settings(set), .en(en), .dest_MUX(dest), .data_MUX(data), .alu_MUX(alu));
  Multiplexer #(.width(8)) multiplexer_5 (
    .in0(reg_file_1_l2), .in1(inst_memory_1_output_code[7:0]), .out(multiplexer_5_out), .sel(rom_1_1_alu_mux));
  reg_file reg_file_2 (
    .Data(multiplexer_4_out), .en(en), .clk(clk), .reset(rst), .W(multiplexer_3_out), .R1(I11t8I),
    .R2(I7t0I), .L1(reg_file_2_l1), .L2(reg_file_2_l2));
  ALU_maison alu_maison_1 (
    .opp(rom_1_1_settings), .INPUT_B(multiplexer_5_out), .INPUT_A(reg_file_1_l1),
    .OUTPUT_ALU(alu_maison_1_output_alu));
  Multiplexer #(.width(8)) multiplexer_6 (
    .in0(reg_file_2_l2), .in1({I7t0I, I3t0I}), .out(multiplexer_6_out), .sel(alu));
  ALU_maison alu_maison_2 (.opp(set), .INPUT_B(multiplexer_6_out), .INPUT_A(reg_file_2_l1), .OUTPUT_ALU(ALU_out));

  // Other names for the same wires on the sheet: I7t0I[3:0] = I3t0I; I7t4I[3:0] = I7t0I
endmodule

module ALU_maison (
  input  [7:0] INPUT_B,
  input  [5:0] opp,
  input  [7:0] INPUT_A,
  output [7:0] OUTPUT_ALU
);

  wire and_2_out, and_3_out, and_4_out, and_5_out, and_6_out, and_7_out, and_8_out, and_9_out, and_10_out,
       and_11_out, and_12_out, and_13_out, and_14_out, and_15_out, and_16_out, and_17_out, and_18_out,
       and_19_out, and_20_out, and_21_out, and_22_out, and_23_out, and_24_out, and_25_out, and_26_out,
       and_27_out, and_28_out, and_29_out, and_30_out, and_31_out, and_32_out, and_33_out, and_34_out,
       and_35_out, and_36_out, and_37_out, and_38_out, and_39_out, and_40_out, and_41_out, and_42_out,
       and_43_out, and_44_out, and_45_out, and_46_out, and_47_out, and_48_out, and_49_out, not_1_out,
       not_2_out, not_3_out, not_4_out, not_5_out, not_6_out, not_7_out, not_8_out, or_8_out, or_16_out,
       or_24_out, R0, R0b, R0c, R1, R1b, R1c, R2, R2b, R2c, R3, R3b, R3c, R4, R4b, R4c, R5, R5b, R5c, R6,
       R6b, R6c, xor_2_out, xor_3_out, xor_4_out, xor_5_out, xor_6_out, xor_7_out, xor_8_out, xor_9_out,
       xor_18_out, xor_19_out, xor_20_out, xor_21_out, xor_22_out, xor_23_out, xor_24_out, xor_25_out,
       xor_34_out, xor_35_out, xor_36_out, xor_37_out, xor_38_out, xor_39_out, xor_40_out, xor_41_out;
  wire [7:0] S_ADD, S_AND, S_NOR, S_RSH, S_SUB, S_XOR;

  Multiplexer #(.select(6), .width(8)) multiplexer_1 (
    .in0(S_ADD), .in1(S_RSH), .in6(S_NOR), .in20(S_XOR), .in24(S_SUB), .in54(S_AND), .out(OUTPUT_ALU),
    .sel(opp));  // open: in2, in3, in4, in5, in7, in8, in9, in10, in11, in12, in13, in14, in15, in16, in17, in18, in19, in21, in22, in23, in25, in26, in27, in28, in29, in30, in31, in32, in33, in34, in35, in36, in37, in38, in39, in40, in41, in42, in43, in44, in45, in46, in47, in48, in49, in50, in51, in52, in53, in55, in56, in57, in58, in59, in60, in61, in62, in63
  assign S_AND = INPUT_A & INPUT_B;  // AND_Gate and_1, 8 bits wide
  assign S_NOR = ~(INPUT_A | INPUT_B);  // NOR_Gate nor_1, 8 bits wide
  assign S_XOR = INPUT_A ^ INPUT_B;  // XOR_Gate xor_1, 8 bits wide
  xor xor_2 (xor_2_out, INPUT_A[0], INPUT_B[0]);
  xor xor_3 (xor_3_out, INPUT_A[1], INPUT_B[1]);
  xor xor_4 (xor_4_out, INPUT_A[2], INPUT_B[2]);
  xor xor_5 (xor_5_out, INPUT_A[3], INPUT_B[3]);
  xor xor_6 (xor_6_out, INPUT_A[4], INPUT_B[4]);
  xor xor_7 (xor_7_out, INPUT_A[5], INPUT_B[5]);
  xor xor_8 (xor_8_out, INPUT_A[6], INPUT_B[6]);
  xor xor_9 (xor_9_out, INPUT_A[7], INPUT_B[7]);
  and and_2 (and_2_out, 1'b0, xor_2_out);
  and and_3 (and_3_out, INPUT_B[0], INPUT_A[0]);
  and and_4 (and_4_out, R0, xor_3_out);
  and and_5 (and_5_out, INPUT_B[1], INPUT_A[1]);
  and and_6 (and_6_out, R1, xor_4_out);
  and and_7 (and_7_out, INPUT_B[2], INPUT_A[2]);
  and and_8 (and_8_out, R2, xor_5_out);
  and and_9 (and_9_out, INPUT_B[3], INPUT_A[3]);
  and and_10 (and_10_out, R3, xor_6_out);
  and and_11 (and_11_out, INPUT_B[4], INPUT_A[4]);
  and and_12 (and_12_out, R4, xor_7_out);
  and and_13 (and_13_out, INPUT_B[5], INPUT_A[5]);
  and and_14 (and_14_out, R5, xor_8_out);
  and and_15 (and_15_out, INPUT_B[6], INPUT_A[6]);
  and and_16 (and_16_out, R6, xor_9_out);
  and and_17 (and_17_out, INPUT_B[7], INPUT_A[7]);
  xor xor_10 (S_ADD[0], xor_2_out, 1'b0);
  or or_1 (R0, and_2_out, and_3_out);
  xor xor_11 (S_ADD[1], xor_3_out, R0);
  or or_2 (R1, and_4_out, and_5_out);
  xor xor_12 (S_ADD[2], xor_4_out, R1);
  or or_3 (R2, and_6_out, and_7_out);
  xor xor_13 (S_ADD[3], xor_5_out, R2);
  or or_4 (R3, and_8_out, and_9_out);
  xor xor_14 (S_ADD[4], xor_6_out, R3);
  or or_5 (R4, and_10_out, and_11_out);
  xor xor_15 (S_ADD[5], xor_7_out, R4);
  or or_6 (R5, and_12_out, and_13_out);
  xor xor_16 (S_ADD[6], xor_8_out, R5);
  or or_7 (R6, and_14_out, and_15_out);
  xor xor_17 (S_ADD[7], xor_9_out, R6);
  or or_8 (or_8_out, and_16_out, and_17_out);
  LED led_1 (.in(or_8_out));
  not not_1 (not_1_out, INPUT_B[0]);
  not not_2 (not_2_out, INPUT_B[1]);
  not not_3 (not_3_out, INPUT_B[2]);
  not not_4 (not_4_out, INPUT_B[3]);
  not not_5 (not_5_out, INPUT_B[4]);
  not not_6 (not_6_out, INPUT_B[5]);
  not not_7 (not_7_out, INPUT_B[6]);
  not not_8 (not_8_out, INPUT_B[7]);
  xor xor_18 (xor_18_out, INPUT_A[0], not_1_out);
  xor xor_19 (xor_19_out, INPUT_A[1], not_2_out);
  xor xor_20 (xor_20_out, INPUT_A[2], not_3_out);
  xor xor_21 (xor_21_out, INPUT_A[3], not_4_out);
  xor xor_22 (xor_22_out, INPUT_A[4], not_5_out);
  xor xor_23 (xor_23_out, INPUT_A[5], not_6_out);
  xor xor_24 (xor_24_out, INPUT_A[6], not_7_out);
  xor xor_25 (xor_25_out, INPUT_A[7], not_8_out);
  xor xor_26 (S_SUB[0], xor_18_out, 1'b1);
  and and_18 (and_18_out, 1'b1, xor_18_out);
  and and_19 (and_19_out, not_1_out, INPUT_A[0]);
  xor xor_27 (S_SUB[1], xor_19_out, R0b);
  and and_20 (and_20_out, R0b, xor_19_out);
  and and_21 (and_21_out, not_2_out, INPUT_A[1]);
  xor xor_28 (S_SUB[2], xor_20_out, R1b);
  and and_22 (and_22_out, R1b, xor_20_out);
  and and_23 (and_23_out, not_3_out, INPUT_A[2]);
  xor xor_29 (S_SUB[3], xor_21_out, R2b);
  and and_24 (and_24_out, R2b, xor_21_out);
  and and_25 (and_25_out, not_4_out, INPUT_A[3]);
  xor xor_30 (S_SUB[4], xor_22_out, R3b);
  and and_26 (and_26_out, R3b, xor_22_out);
  and and_27 (and_27_out, not_5_out, INPUT_A[4]);
  xor xor_31 (S_SUB[5], xor_23_out, R4b);
  and and_28 (and_28_out, R4b, xor_23_out);
  and and_29 (and_29_out, not_6_out, INPUT_A[5]);
  xor xor_32 (S_SUB[6], xor_24_out, R5b);
  and and_30 (and_30_out, R5b, xor_24_out);
  and and_31 (and_31_out, not_7_out, INPUT_A[6]);
  xor xor_33 (S_SUB[7], xor_25_out, R6b);
  and and_32 (and_32_out, R6b, xor_25_out);
  and and_33 (and_33_out, not_8_out, INPUT_A[7]);
  or or_9 (R0b, and_18_out, and_19_out);
  or or_10 (R1b, and_20_out, and_21_out);
  or or_11 (R2b, and_22_out, and_23_out);
  or or_12 (R3b, and_24_out, and_25_out);
  or or_13 (R4b, and_26_out, and_27_out);
  or or_14 (R5b, and_28_out, and_29_out);
  or or_15 (R6b, and_30_out, and_31_out);
  or or_16 (or_16_out, and_32_out, and_33_out);
  LED led_2 (.in(or_16_out));
  xor xor_34 (xor_34_out, INPUT_A[0], INPUT_A[0]);
  xor xor_35 (xor_35_out, INPUT_A[1], INPUT_A[1]);
  xor xor_36 (xor_36_out, INPUT_A[2], INPUT_A[2]);
  xor xor_37 (xor_37_out, INPUT_A[3], INPUT_A[3]);
  xor xor_38 (xor_38_out, INPUT_A[4], INPUT_A[4]);
  xor xor_39 (xor_39_out, INPUT_A[5], INPUT_A[5]);
  xor xor_40 (xor_40_out, INPUT_A[6], INPUT_A[6]);
  xor xor_41 (xor_41_out, INPUT_A[7], INPUT_A[7]);
  xor xor_42 (S_RSH[0], xor_34_out, 1'b0);
  and and_34 (and_34_out, 1'b0, xor_34_out);
  and and_35 (and_35_out, INPUT_A[0], INPUT_A[0]);
  xor xor_43 (S_RSH[1], xor_35_out, R0c);
  and and_36 (and_36_out, R0c, xor_35_out);
  and and_37 (and_37_out, INPUT_A[1], INPUT_A[1]);
  xor xor_44 (S_RSH[2], xor_36_out, R1c);
  and and_38 (and_38_out, R1c, xor_36_out);
  and and_39 (and_39_out, INPUT_A[2], INPUT_A[2]);
  xor xor_45 (S_RSH[3], xor_37_out, R2c);
  and and_40 (and_40_out, R2c, xor_37_out);
  and and_41 (and_41_out, INPUT_A[3], INPUT_A[3]);
  xor xor_46 (S_RSH[4], xor_38_out, R3c);
  and and_42 (and_42_out, R3c, xor_38_out);
  and and_43 (and_43_out, INPUT_A[4], INPUT_A[4]);
  xor xor_47 (S_RSH[5], xor_39_out, R4c);
  and and_44 (and_44_out, R4c, xor_39_out);
  and and_45 (and_45_out, INPUT_A[5], INPUT_A[5]);
  xor xor_48 (S_RSH[6], xor_40_out, R5c);
  and and_46 (and_46_out, R5c, xor_40_out);
  and and_47 (and_47_out, INPUT_A[6], INPUT_A[6]);
  xor xor_49 (S_RSH[7], xor_41_out, R6c);
  and and_48 (and_48_out, R6c, xor_41_out);
  and and_49 (and_49_out, INPUT_A[7], INPUT_A[7]);
  or or_17 (R0c, and_34_out, and_35_out);
  or or_18 (R1c, and_36_out, and_37_out);
  or or_19 (R2c, and_38_out, and_39_out);
  or or_20 (R3c, and_40_out, and_41_out);
  or or_21 (R4c, and_42_out, and_43_out);
  or or_22 (R5c, and_44_out, and_45_out);
  or or_23 (R6c, and_46_out, and_47_out);
  or or_24 (or_24_out, and_48_out, and_49_out);
  LED led_3 (.in(or_24_out));

  // Other names for the same wires on the sheet: N1[7:0] = INPUT_A; N1_0 = INPUT_A[0]; N1_1 = INPUT_A[1];
  //   N1_2 = INPUT_A[2]; N1_3 = INPUT_A[3]; N1_4 = INPUT_A[4]; N1_5 = INPUT_A[5]; N1_6 = INPUT_A[6];
  //   N1_7 = INPUT_A[7]; N2[7:0] = INPUT_B; N2_0 = INPUT_B[0]; N2_1 = INPUT_B[1]; N2_2 = INPUT_B[2];
  //   N2_3 = INPUT_B[3]; N2_4 = INPUT_B[4]; N2_5 = INPUT_B[5]; N2_6 = INPUT_B[6]; N2_7 = INPUT_B[7]
endmodule

module reg_file (
  input  [3:0] W,
  input  [3:0] R1,
  input  [3:0] R2,
  input  [7:0] Data,
  input  en,
  input  clk,
  input  reset,
  output [7:0] L1,
  output [7:0] L2
);

  wire E1, E2, E3, E4, E5, E6, E7, E8, E9, E10, E11, E12, E13, E14, E15;
  wire [3:0] READ1, READ2, WRITE;
  wire [7:0] bit_in, L1_1, L1_2, L1_3, L1_4, L1_5, L1_6, L1_7, L1_8, L1_9, L1_10, L1_11, L1_12, L1_13, L1_14,
       L1_15, L2_1, L2_2, L2_3, L2_4, L2_5, L2_6, L2_7, L2_8, L2_9, L2_10, L2_11, L2_12, L2_13, L2_14, L2_15;

  assign WRITE = en ? W : 4'bz;  // Controlled_Buffer controlled_buffer_1
  assign READ1 = en ? R1 : 4'bz;  // Controlled_Buffer controlled_buffer_2
  assign READ2 = en ? R2 : 4'bz;  // Controlled_Buffer controlled_buffer_3
  assign bit_in = en ? Data : 8'bz;  // Controlled_Buffer controlled_buffer_4
  Register register_1 (.D(bit_in), .en(E1), .clk(clk), .Q(L1_1), .clr(reset));
  Register register_2 (.D(bit_in), .en(E2), .clk(clk), .Q(L1_2), .clr(reset));
  Register register_3 (.D(bit_in), .en(E3), .clk(clk), .Q(L1_3), .clr(reset));
  Register register_4 (.D(bit_in), .en(E4), .clk(clk), .Q(L1_4), .clr(reset));
  Register register_5 (.D(bit_in), .en(E5), .clk(clk), .Q(L1_5), .clr(reset));
  Register register_6 (.D(bit_in), .en(E6), .clk(clk), .Q(L1_6), .clr(reset));
  Register register_7 (.D(bit_in), .en(E7), .clk(clk), .Q(L1_7), .clr(reset));
  Register register_8 (.D(bit_in), .en(E8), .clk(clk), .Q(L1_8), .clr(reset));
  Register register_9 (.D(bit_in), .en(E9), .clk(clk), .Q(L1_9), .clr(reset));
  Register register_10 (.D(bit_in), .en(E10), .clk(clk), .Q(L1_10), .clr(reset));
  Register register_11 (.D(bit_in), .en(E11), .clk(clk), .Q(L1_11), .clr(reset));
  Register register_12 (.D(bit_in), .en(E12), .clk(clk), .Q(L1_12), .clr(reset));
  Register register_13 (.D(bit_in), .en(E13), .clk(clk), .Q(L1_13), .clr(reset));
  Register register_14 (.D(bit_in), .en(E14), .clk(clk), .Q(L1_14), .clr(reset));
  Register register_15 (.D(bit_in), .en(E15), .clk(clk), .Q(L1_15), .clr(reset));
  Register register_16 (.D(bit_in), .en(E1), .clk(clk), .Q(L2_1), .clr(reset));
  Register register_17 (.D(bit_in), .en(E2), .clk(clk), .Q(L2_2), .clr(reset));
  Register register_18 (.D(bit_in), .en(E3), .clk(clk), .Q(L2_3), .clr(reset));
  Register register_19 (.D(bit_in), .en(E4), .clk(clk), .Q(L2_4), .clr(reset));
  Register register_20 (.D(bit_in), .en(E5), .clk(clk), .Q(L2_5), .clr(reset));
  Register register_21 (.D(bit_in), .en(E6), .clk(clk), .Q(L2_6), .clr(reset));
  Register register_22 (.D(bit_in), .en(E7), .clk(clk), .Q(L2_7), .clr(reset));
  Register register_23 (.D(bit_in), .en(E8), .clk(clk), .Q(L2_8), .clr(reset));
  Register register_24 (.D(bit_in), .en(E9), .clk(clk), .Q(L2_9), .clr(reset));
  Register register_25 (.D(bit_in), .en(E10), .clk(clk), .Q(L2_10), .clr(reset));
  Register register_26 (.D(bit_in), .en(E11), .clk(clk), .Q(L2_11), .clr(reset));
  Register register_27 (.D(bit_in), .en(E12), .clk(clk), .Q(L2_12), .clr(reset));
  Register register_28 (.D(bit_in), .en(E13), .clk(clk), .Q(L2_13), .clr(reset));
  Register register_29 (.D(bit_in), .en(E14), .clk(clk), .Q(L2_14), .clr(reset));
  Register register_30 (.D(bit_in), .en(E15), .clk(clk), .Q(L2_15), .clr(reset));
  Decoder #(.select(4)) decoder_1 (
    .out1(E1), .out2(E2), .out3(E3), .out4(E4), .out5(E5), .out6(E6), .out7(E7), .out8(E8), .out9(E9),
    .out10(E10), .out11(E11), .out12(E12), .out13(E13), .out14(E14), .out15(E15), .sel(WRITE));  // open: out0, en
  Multiplexer #(.select(4), .width(8)) multiplexer_1 (
    .in1(L1_1), .in2(L1_2), .in3(L1_3), .in4(L1_4), .in5(L1_5), .in6(L1_6), .in7(L1_7), .in8(L1_8),
    .in9(L1_9), .in10(L1_10), .in11(L1_11), .in12(L1_12), .in13(L1_13), .in14(L1_14), .in15(L1_15), .out(L1),
    .sel(READ1));  // open: in0
  Multiplexer #(.select(4), .width(8)) multiplexer_2 (
    .in1(L2_1), .in2(L2_2), .in3(L2_3), .in4(L2_4), .in5(L2_5), .in6(L2_6), .in7(L2_7), .in8(L2_8),
    .in9(L2_9), .in10(L2_10), .in11(L2_11), .in12(L2_12), .in13(L2_13), .in14(L2_14), .in15(L2_15), .out(L2),
    .sel(READ2));  // open: in0

  // Other names for the same wires on the sheet: LEC1[7:0] = L1; LEC2[7:0] = L2
endmodule

module clock_maison (
  input  clk,
  input  reset,
  input  run,
  input  halt_0,
  input  jumpif_0,
  input  jump_0,
  input  [7:0] bit_in,
  output [5:0] value_clk
);

  wire and_1_out, and_2_out, and_3_out, and_4_out, and_5_out, and_6_out, and_7_out, and_8_out, and_9_out,
       and_10_out, and_11_out, and_12_out, and_13_out, CLK_t, jump, multiplexer_1_out, multiplexer_2_out,
       multiplexer_3_out, multiplexer_4_out, multiplexer_5_out, multiplexer_6_out, or_7_out, R1, R2, R3, R4,
       R5, R6, S0, S1, S2, S3, S4, S5, start, xor_1_out, xor_2_out, xor_3_out, xor_4_out, xor_5_out,
       xor_6_out;

  xor xor_1 (xor_1_out, 1'b1, value_clk[0]);
  xor xor_2 (xor_2_out, 1'b0, value_clk[1]);
  xor xor_3 (xor_3_out, 1'b0, value_clk[2]);
  xor xor_4 (xor_4_out, 1'b0, value_clk[3]);
  xor xor_5 (xor_5_out, 1'b0, value_clk[4]);
  xor xor_6 (xor_6_out, 1'b0, value_clk[5]);
  xor xor_7 (S0, xor_1_out, 1'b0);
  and and_1 (and_1_out, 1'b0, xor_1_out);
  and and_2 (and_2_out, 1'b1, value_clk[0]);
  xor xor_8 (S1, xor_2_out, R1);
  and and_3 (and_3_out, R1, xor_2_out);
  and and_4 (and_4_out, 1'b0, value_clk[1]);
  xor xor_9 (S2, xor_3_out, R2);
  and and_5 (and_5_out, R2, xor_3_out);
  and and_6 (and_6_out, 1'b0, value_clk[2]);
  xor xor_10 (S3, xor_4_out, R3);
  and and_7 (and_7_out, R3, xor_4_out);
  and and_8 (and_8_out, 1'b0, value_clk[3]);
  xor xor_11 (S4, xor_5_out, R4);
  and and_9 (and_9_out, R4, xor_5_out);
  and and_10 (and_10_out, 1'b0, value_clk[4]);
  xor xor_12 (S5, xor_6_out, R5);
  and and_11 (and_11_out, R5, xor_6_out);
  and and_12 (and_12_out, 1'b0, value_clk[5]);
  or or_1 (R1, and_1_out, and_2_out);
  or or_2 (R2, and_3_out, and_4_out);
  or or_3 (R3, and_5_out, and_6_out);
  or or_4 (R4, and_7_out, and_8_out);
  or or_5 (R5, and_9_out, and_10_out);
  or or_6 (R6, and_11_out, and_12_out);
  Multiplexer multiplexer_1 (.in0(S0), .in1(bit_in[0]), .out(multiplexer_1_out), .sel(jump));
  D_Flip_Flop d_ff_1 (.D(multiplexer_1_out), .clk(CLK_t), .Q(value_clk[0]), .reset(reset));  // open: Qn, preset
  Multiplexer multiplexer_2 (.in0(S1), .in1(bit_in[1]), .out(multiplexer_2_out), .sel(jump));
  D_Flip_Flop d_ff_2 (.D(multiplexer_2_out), .clk(CLK_t), .Q(value_clk[1]), .reset(reset));  // open: Qn, preset
  Multiplexer multiplexer_3 (.in0(S2), .in1(bit_in[2]), .out(multiplexer_3_out), .sel(jump));
  D_Flip_Flop d_ff_3 (.D(multiplexer_3_out), .clk(CLK_t), .Q(value_clk[2]), .reset(reset));  // open: Qn, preset
  Multiplexer multiplexer_4 (.in0(S3), .in1(bit_in[3]), .out(multiplexer_4_out), .sel(jump));
  D_Flip_Flop d_ff_4 (.D(multiplexer_4_out), .clk(CLK_t), .Q(value_clk[3]), .reset(reset));  // open: Qn, preset
  Multiplexer multiplexer_5 (.in0(S4), .in1(bit_in[4]), .out(multiplexer_5_out), .sel(jump));
  D_Flip_Flop d_ff_5 (.D(multiplexer_5_out), .clk(CLK_t), .Q(value_clk[4]), .reset(reset));  // open: Qn, preset
  Multiplexer multiplexer_6 (.in0(S5), .in1(bit_in[5]), .out(multiplexer_6_out), .sel(jump));
  D_Flip_Flop d_ff_6 (.D(multiplexer_6_out), .clk(CLK_t), .Q(value_clk[5]), .reset(reset));  // open: Qn, preset
  D_Flip_Flop d_ff_7 (.D(run), .clk(run), .Q(start), .reset(or_7_out));  // open: Qn, preset
  or or_7 (or_7_out, halt_0, and_13_out, reset);
  and and_13 (and_13_out, R5, value_clk[5], value_clk[4], value_clk[3], value_clk[2], value_clk[1], value_clk[0]);
  and and_14 (CLK_t, clk, start);
  or or_8 (jump, jumpif_0, jump_0);

  // Other names for the same wires on the sheet: J0 = bit_in[0]; J1 = bit_in[1]; J2 = bit_in[2]; J3 = bit_in[3];
  //   J4 = bit_in[4]; J5 = bit_in[5]; J6 = bit_in[6]; J7 = bit_in[7]; halt = halt_0; A0 = value_clk[0];
  //   A1 = value_clk[1]; A2 = value_clk[2]; A3 = value_clk[3]; A4 = value_clk[4]; A5 = value_clk[5]
endmodule

module inst_memory (
  input  load,
  input  reset,
  input  [9:0] addr,
  output [15:0] output_code
);

  wire [15:0] S0, S1, S2, S3, S4, S5, S6, S7, S8, S9, S10, S11, S12, S13, S14, S15, S16, S17, S18, S19, S20,
       S21, S22, S23, S24, S25, S26, S27, S28, S29, S30, S31, S32, S33, S34, S35, S36, S37, S38, S39, S40,
       S41, S42, S43, S44, S45, S46, S47, S48, S49, S50, S51, S52, S53, S54, S55, S56, S57, S58, S59, S60,
       S61, S62, S63, undriven, undriven_2, undriven_3, undriven_4, undriven_5, undriven_6, undriven_7,
       undriven_8, undriven_9, undriven_10, undriven_11, undriven_12, undriven_13, undriven_14, undriven_15,
       undriven_16, undriven_17, undriven_18, undriven_19, undriven_20, undriven_21, undriven_22,
       undriven_23, undriven_24, undriven_25, undriven_26, undriven_27, undriven_28, undriven_29,
       undriven_30, undriven_31, undriven_32, undriven_33, undriven_34, undriven_35, undriven_36,
       undriven_37, undriven_38, undriven_39, undriven_40, undriven_41, undriven_42, undriven_43,
       undriven_44, undriven_45, undriven_46, undriven_47, undriven_48, undriven_49, undriven_50,
       undriven_51, undriven_52, undriven_53, undriven_54, undriven_55, undriven_56, undriven_57,
       undriven_58, undriven_59, undriven_60, undriven_61, undriven_62, undriven_63, undriven_64;

  // DipSwitch #(.number(16)) dipswitch_1: pin names not known
  Register #(.width(16)) register_1 (.D(undriven), .en(load), .clk(load), .Q(S0), .clr(reset));
  // DipSwitch #(.number(16)) dipswitch_2: pin names not known
  Register #(.width(16)) register_2 (.D(undriven_2), .en(load), .clk(load), .Q(S8), .clr(reset));
  // DipSwitch #(.number(16)) dipswitch_3: pin names not known
  Register #(.width(16)) register_3 (.D(undriven_3), .en(load), .clk(load), .Q(S16), .clr(reset));
  // DipSwitch #(.number(16)) dipswitch_4: pin names not known
  Register #(.width(16)) register_4 (.D(undriven_4), .en(load), .clk(load), .Q(S24), .clr(reset));
  // DipSwitch #(.number(16)) dipswitch_5: pin names not known
  Register #(.width(16)) register_5 (.D(undriven_5), .en(load), .clk(load), .Q(S32), .clr(reset));
  // DipSwitch #(.number(16)) dipswitch_6: pin names not known
  Register #(.width(16)) register_6 (.D(undriven_6), .en(load), .clk(load), .Q(S40), .clr(reset));
  // DipSwitch #(.number(16)) dipswitch_7: pin names not known
  Register #(.width(16)) register_7 (.D(undriven_7), .en(load), .clk(load), .Q(S48), .clr(reset));
  // DipSwitch #(.number(16)) dipswitch_8: pin names not known
  Register #(.width(16)) register_8 (.D(undriven_8), .en(load), .clk(load), .Q(S56), .clr(reset));
  // DipSwitch #(.number(16)) dipswitch_9: pin names not known
  Register #(.width(16)) register_9 (.D(undriven_9), .en(load), .clk(load), .Q(S1), .clr(reset));
  // DipSwitch #(.number(16)) dipswitch_10: pin names not known
  Register #(.width(16)) register_10 (.D(undriven_10), .en(load), .clk(load), .Q(S9), .clr(reset));
  // DipSwitch #(.number(16)) dipswitch_11: pin names not known
  Register #(.width(16)) register_11 (.D(undriven_11), .en(load), .clk(load), .Q(S17), .clr(reset));
  // DipSwitch #(.number(16)) dipswitch_12: pin names not known
  Register #(.width(16)) register_12 (.D(undriven_12), .en(load), .clk(load), .Q(S25), .clr(reset));
  // DipSwitch #(.number(16)) dipswitch_13: pin names not known
  Register #(.width(16)) register_13 (.D(undriven_13), .en(load), .clk(load), .Q(S33), .clr(reset));
  // DipSwitch #(.number(16)) dipswitch_14: pin names not known
  Register #(.width(16)) register_14 (.D(undriven_14), .en(load), .clk(load), .Q(S41), .clr(reset));
  // DipSwitch #(.number(16)) dipswitch_15: pin names not known
  Register #(.width(16)) register_15 (.D(undriven_15), .en(load), .clk(load), .Q(S49), .clr(reset));
  // DipSwitch #(.number(16)) dipswitch_16: pin names not known
  Register #(.width(16)) register_16 (.D(undriven_16), .en(load), .clk(load), .Q(S57), .clr(reset));
  // DipSwitch #(.number(16)) dipswitch_17: pin names not known
  Register #(.width(16)) register_17 (.D(undriven_17), .en(load), .clk(load), .Q(S2), .clr(reset));
  // DipSwitch #(.number(16)) dipswitch_18: pin names not known
  Register #(.width(16)) register_18 (.D(undriven_18), .en(load), .clk(load), .Q(S10), .clr(reset));
  // DipSwitch #(.number(16)) dipswitch_19: pin names not known
  Register #(.width(16)) register_19 (.D(undriven_19), .en(load), .clk(load), .Q(S18), .clr(reset));
  // DipSwitch #(.number(16)) dipswitch_20: pin names not known
  Register #(.width(16)) register_20 (.D(undriven_20), .en(load), .clk(load), .Q(S26), .clr(reset));
  // DipSwitch #(.number(16)) dipswitch_21: pin names not known
  Register #(.width(16)) register_21 (.D(undriven_21), .en(load), .clk(load), .Q(S34), .clr(reset));
  // DipSwitch #(.number(16)) dipswitch_22: pin names not known
  Register #(.width(16)) register_22 (.D(undriven_22), .en(load), .clk(load), .Q(S42), .clr(reset));
  // DipSwitch #(.number(16)) dipswitch_23: pin names not known
  Register #(.width(16)) register_23 (.D(undriven_23), .en(load), .clk(load), .Q(S50), .clr(reset));
  // DipSwitch #(.number(16)) dipswitch_24: pin names not known
  Register #(.width(16)) register_24 (.D(undriven_24), .en(load), .clk(load), .Q(S58), .clr(reset));
  // DipSwitch #(.number(16)) dipswitch_25: pin names not known
  Register #(.width(16)) register_25 (.D(undriven_25), .en(load), .clk(load), .Q(S3), .clr(reset));
  // DipSwitch #(.number(16)) dipswitch_26: pin names not known
  Register #(.width(16)) register_26 (.D(undriven_26), .en(load), .clk(load), .Q(S11), .clr(reset));
  // DipSwitch #(.number(16)) dipswitch_27: pin names not known
  Register #(.width(16)) register_27 (.D(undriven_27), .en(load), .clk(load), .Q(S19), .clr(reset));
  // DipSwitch #(.number(16)) dipswitch_28: pin names not known
  Register #(.width(16)) register_28 (.D(undriven_28), .en(load), .clk(load), .Q(S27), .clr(reset));
  // DipSwitch #(.number(16)) dipswitch_29: pin names not known
  Register #(.width(16)) register_29 (.D(undriven_29), .en(load), .clk(load), .Q(S35), .clr(reset));
  // DipSwitch #(.number(16)) dipswitch_30: pin names not known
  Register #(.width(16)) register_30 (.D(undriven_30), .en(load), .clk(load), .Q(S43), .clr(reset));
  // DipSwitch #(.number(16)) dipswitch_31: pin names not known
  Register #(.width(16)) register_31 (.D(undriven_31), .en(load), .clk(load), .Q(S51), .clr(reset));
  // DipSwitch #(.number(16)) dipswitch_32: pin names not known
  Register #(.width(16)) register_32 (.D(undriven_32), .en(load), .clk(load), .Q(S59), .clr(reset));
  Multiplexer #(.select(6), .width(16)) multiplexer_1 (
    .in0(S0), .in1(S1), .in2(S2), .in3(S3), .in4(S4), .in5(S5), .in6(S6), .in7(S7), .in8(S8), .in9(S9),
    .in10(S10), .in11(S11), .in12(S12), .in13(S13), .in14(S14), .in15(S15), .in16(S16), .in17(S17),
    .in18(S18), .in19(S19), .in20(S20), .in21(S21), .in22(S22), .in23(S23), .in24(S24), .in25(S25),
    .in26(S26), .in27(S27), .in28(S28), .in29(S29), .in30(S30), .in31(S31), .in32(S32), .in33(S33),
    .in34(S34), .in35(S35), .in36(S36), .in37(S37), .in38(S38), .in39(S39), .in40(S40), .in41(S41),
    .in42(S42), .in43(S43), .in44(S44), .in45(S45), .in46(S46), .in47(S47), .in48(S48), .in49(S49),
    .in50(S50), .in51(S51), .in52(S52), .in53(S53), .in54(S54), .in55(S55), .in56(S56), .in57(S57),
    .in58(S58), .in59(S59), .in60(S60), .in61(S61), .in62(S62), .in63(S63), .out(output_code), .sel(addr[5:0]));
  // DipSwitch #(.number(16)) dipswitch_33: pin names not known
  Register #(.width(16)) register_33 (.D(undriven_33), .en(load), .clk(load), .Q(S4), .clr(reset));
  // DipSwitch #(.number(16)) dipswitch_34: pin names not known
  Register #(.width(16)) register_34 (.D(undriven_34), .en(load), .clk(load), .Q(S12), .clr(reset));
  // DipSwitch #(.number(16)) dipswitch_35: pin names not known
  Register #(.width(16)) register_35 (.D(undriven_35), .en(load), .clk(load), .Q(S20), .clr(reset));
  // DipSwitch #(.number(16)) dipswitch_36: pin names not known
  Register #(.width(16)) register_36 (.D(undriven_36), .en(load), .clk(load), .Q(S28), .clr(reset));
  // DipSwitch #(.number(16)) dipswitch_37: pin names not known
  Register #(.width(16)) register_37 (.D(undriven_37), .en(load), .clk(load), .Q(S36), .clr(reset));
  // DipSwitch #(.number(16)) dipswitch_38: pin names not known
  Register #(.width(16)) register_38 (.D(undriven_38), .en(load), .clk(load), .Q(S44), .clr(reset));
  // DipSwitch #(.number(16)) dipswitch_39: pin names not known
  Register #(.width(16)) register_39 (.D(undriven_39), .en(load), .clk(load), .Q(S52), .clr(reset));
  // DipSwitch #(.number(16)) dipswitch_40: pin names not known
  Register #(.width(16)) register_40 (.D(undriven_40), .en(load), .clk(load), .Q(S60), .clr(reset));
  // DipSwitch #(.number(16)) dipswitch_41: pin names not known
  Register #(.width(16)) register_41 (.D(undriven_41), .en(load), .clk(load), .Q(S5), .clr(reset));
  // DipSwitch #(.number(16)) dipswitch_42: pin names not known
  Register #(.width(16)) register_42 (.D(undriven_42), .en(load), .clk(load), .Q(S13), .clr(reset));
  // DipSwitch #(.number(16)) dipswitch_43: pin names not known
  Register #(.width(16)) register_43 (.D(undriven_43), .en(load), .clk(load), .Q(S21), .clr(reset));
  // DipSwitch #(.number(16)) dipswitch_44: pin names not known
  Register #(.width(16)) register_44 (.D(undriven_44), .en(load), .clk(load), .Q(S29), .clr(reset));
  // DipSwitch #(.number(16)) dipswitch_45: pin names not known
  Register #(.width(16)) register_45 (.D(undriven_45), .en(load), .clk(load), .Q(S37), .clr(reset));
  // DipSwitch #(.number(16)) dipswitch_46: pin names not known
  Register #(.width(16)) register_46 (.D(undriven_46), .en(load), .clk(load), .Q(S45), .clr(reset));
  // DipSwitch #(.number(16)) dipswitch_47: pin names not known
  Register #(.width(16)) register_47 (.D(undriven_47), .en(load), .clk(load), .Q(S53), .clr(reset));
  // DipSwitch #(.number(16)) dipswitch_48: pin names not known
  Register #(.width(16)) register_48 (.D(undriven_48), .en(load), .clk(load), .Q(S61), .clr(reset));
  // DipSwitch #(.number(16)) dipswitch_49: pin names not known
  Register #(.width(16)) register_49 (.D(undriven_49), .en(load), .clk(load), .Q(S6), .clr(reset));
  // DipSwitch #(.number(16)) dipswitch_50: pin names not known
  Register #(.width(16)) register_50 (.D(undriven_50), .en(load), .clk(load), .Q(S14), .clr(reset));
  // DipSwitch #(.number(16)) dipswitch_51: pin names not known
  Register #(.width(16)) register_51 (.D(undriven_51), .en(load), .clk(load), .Q(S22), .clr(reset));
  // DipSwitch #(.number(16)) dipswitch_52: pin names not known
  Register #(.width(16)) register_52 (.D(undriven_52), .en(load), .clk(load), .Q(S30), .clr(reset));
  // DipSwitch #(.number(16)) dipswitch_53: pin names not known
  // DipSwitch #(.number(16)) dipswitch_54: pin names not known
  // DipSwitch #(.number(16)) dipswitch_55: pin names not known
  // DipSwitch #(.number(16)) dipswitch_56: pin names not known
  Register #(.width(16)) register_53 (.D(undriven_53), .en(load), .clk(load), .Q(S38), .clr(reset));
  Register #(.width(16)) register_54 (.D(undriven_54), .en(load), .clk(load), .Q(S46), .clr(reset));
  Register #(.width(16)) register_55 (.D(undriven_55), .en(load), .clk(load), .Q(S54), .clr(reset));
  Register #(.width(16)) register_56 (.D(undriven_56), .en(load), .clk(load), .Q(S62), .clr(reset));
  // DipSwitch #(.number(16)) dipswitch_57: pin names not known
  // DipSwitch #(.number(16)) dipswitch_58: pin names not known
  // DipSwitch #(.number(16)) dipswitch_59: pin names not known
  // DipSwitch #(.number(16)) dipswitch_60: pin names not known
  Register #(.width(16)) register_57 (.D(undriven_57), .en(load), .clk(load), .Q(S7), .clr(reset));
  Register #(.width(16)) register_58 (.D(undriven_58), .en(load), .clk(load), .Q(S15), .clr(reset));
  Register #(.width(16)) register_59 (.D(undriven_59), .en(load), .clk(load), .Q(S23), .clr(reset));
  Register #(.width(16)) register_60 (.D(undriven_60), .en(load), .clk(load), .Q(S31), .clr(reset));
  // DipSwitch #(.number(16)) dipswitch_61: pin names not known
  Register #(.width(16)) register_61 (.D(undriven_61), .en(load), .clk(load), .Q(S39), .clr(reset));
  // DipSwitch #(.number(16)) dipswitch_62: pin names not known
  Register #(.width(16)) register_62 (.D(undriven_62), .en(load), .clk(load), .Q(S47), .clr(reset));
  // DipSwitch #(.number(16)) dipswitch_63: pin names not known
  Register #(.width(16)) register_63 (.D(undriven_63), .en(load), .clk(load), .Q(S55), .clr(reset));
  // DipSwitch #(.number(16)) dipswitch_64: pin names not known
  Register #(.width(16)) register_64 (.D(undriven_64), .en(load), .clk(load), .Q(S63), .clr(reset));

  // Other names for the same wires on the sheet: value_clk[5:0] = addr[5:0]
endmodule

module Program_Counter (
  input  [9:0] addr,
  input  clk,
  input  rst,
  output [9:0] out_4
);

  Register #(.width(10)) register_1 (.D(addr), .clk(clk), .Q(out_4), .clr(rst));  // open: en
endmodule

module add_1 (
  input  [9:0] INPUT_A,
  input  [9:0] INPUT_B,
  output [9:0] out_3
);

  wire and_1_out, and_2_out, and_3_out, and_4_out, and_5_out, and_6_out, and_7_out, and_8_out, and_9_out,
       and_10_out, and_11_out, and_12_out, and_13_out, and_14_out, and_15_out, and_16_out, and_17_out,
       and_18_out, and_19_out, and_20_out, or_10_out, R0, R1, R2, R3, R4, R5, R6, R7, R8, xor_1_out,
       xor_2_out, xor_3_out, xor_4_out, xor_5_out, xor_6_out, xor_7_out, xor_8_out, xor_9_out, xor_10_out;

  xor xor_1 (xor_1_out, INPUT_A[0], INPUT_B[0]);
  xor xor_2 (xor_2_out, INPUT_A[1], INPUT_B[1]);
  xor xor_3 (xor_3_out, INPUT_A[2], INPUT_B[2]);
  xor xor_4 (xor_4_out, INPUT_A[3], INPUT_B[3]);
  xor xor_5 (xor_5_out, INPUT_A[4], INPUT_B[4]);
  xor xor_6 (xor_6_out, INPUT_A[5], INPUT_B[5]);
  xor xor_7 (xor_7_out, INPUT_A[6], INPUT_B[6]);
  xor xor_8 (xor_8_out, INPUT_A[7], INPUT_B[7]);
  xor xor_9 (xor_9_out, INPUT_A[8], INPUT_B[8]);
  xor xor_10 (xor_10_out, INPUT_A[9], INPUT_B[9]);
  xor xor_11 (out_3[0], xor_1_out, 1'b0);
  and and_1 (and_1_out, 1'b0, xor_1_out);
  and and_2 (and_2_out, INPUT_B[0], INPUT_A[0]);
  xor xor_12 (out_3[1], xor_2_out, R0);
  and and_3 (and_3_out, R0, xor_2_out);
  and and_4 (and_4_out, INPUT_B[1], INPUT_A[1]);
  xor xor_13 (out_3[2], xor_3_out, R1);
  and and_5 (and_5_out, R1, xor_3_out);
  and and_6 (and_6_out, INPUT_B[2], INPUT_A[2]);
  xor xor_14 (out_3[3], xor_4_out, R2);
  and and_7 (and_7_out, R2, xor_4_out);
  and and_8 (and_8_out, INPUT_B[3], INPUT_A[3]);
  xor xor_15 (out_3[4], xor_5_out, R3);
  and and_9 (and_9_out, R3, xor_5_out);
  and and_10 (and_10_out, INPUT_B[4], INPUT_A[4]);
  xor xor_16 (out_3[5], xor_6_out, R4);
  and and_11 (and_11_out, R4, xor_6_out);
  and and_12 (and_12_out, INPUT_B[5], INPUT_A[5]);
  xor xor_17 (out_3[6], xor_7_out, R5);
  and and_13 (and_13_out, R5, xor_7_out);
  and and_14 (and_14_out, INPUT_B[6], INPUT_A[6]);
  xor xor_18 (out_3[7], xor_8_out, R6);
  and and_15 (and_15_out, R6, xor_8_out);
  and and_16 (and_16_out, INPUT_B[7], INPUT_A[7]);
  xor xor_19 (out_3[8], xor_9_out, R7);
  and and_17 (and_17_out, R7, xor_9_out);
  and and_18 (and_18_out, INPUT_B[8], INPUT_A[8]);
  xor xor_20 (out_3[9], xor_10_out, R8);
  and and_19 (and_19_out, R8, xor_10_out);
  and and_20 (and_20_out, INPUT_B[9], INPUT_A[9]);
  or or_1 (R0, and_1_out, and_2_out);
  or or_2 (R1, and_3_out, and_4_out);
  or or_3 (R2, and_5_out, and_6_out);
  or or_4 (R3, and_7_out, and_8_out);
  or or_5 (R4, and_9_out, and_10_out);
  or or_6 (R5, and_11_out, and_12_out);
  or or_7 (R6, and_13_out, and_14_out);
  or or_8 (R7, and_15_out, and_16_out);
  or or_9 (R8, and_17_out, and_18_out);
  or or_10 (or_10_out, and_19_out, and_20_out);
  LED led_1 (.in(or_10_out));

  // Other names for the same wires on the sheet: N1_0 = INPUT_A[0]; N1_1 = INPUT_A[1]; N1_2 = INPUT_A[2];
  //   N1_3 = INPUT_A[3]; N1_4 = INPUT_A[4]; N1_5 = INPUT_A[5]; N1_6 = INPUT_A[6]; N1_7 = INPUT_A[7];
  //   N1_8 = INPUT_A[8]; N1_9 = INPUT_A[9]; N2_0 = INPUT_B[0]; N2_1 = INPUT_B[1]; N2_2 = INPUT_B[2];
  //   N2_3 = INPUT_B[3]; N2_4 = INPUT_B[4]; N2_5 = INPUT_B[5]; N2_6 = INPUT_B[6]; N2_7 = INPUT_B[7];
  //   N2_8 = INPUT_B[8]; N2_9 = INPUT_B[9]
endmodule

module ROM_1 (
  input  [3:0] op_code,
  output en,
  output dest_MUX,
  output [5:0] settings,
  output data_MUX,
  output alu_MUX
);

  wire and_2_out, not_1_out, not_2_out, not_3_out, not_4_out, not_5_out, not_6_out;
  wire [6:6] multiplexer_1_out;

  Multiplexer #(.select(4), .width(7)) multiplexer_1 (
    .in2(7'b1000000), .in3(7'b1011000), .in4(7'b1000110), .in5(7'b1110110), .in6(7'b1010100),
    .in7(7'b1000001), .in9(7'b1000000), .out({multiplexer_1_out[6], settings}), .sel(op_code));  // open: in0, in1, in8, in10, in11, in12, in13, in14, in15
  or or_1 (en, multiplexer_1_out[6], data_MUX);
  not not_1 (not_1_out, op_code[0]);
  not not_2 (not_2_out, op_code[2]);
  not not_3 (not_3_out, op_code[3]);
  not not_4 (not_4_out, op_code[2]);
  not not_5 (not_5_out, op_code[1]);
  not not_6 (not_6_out, op_code[1]);
  or or_2 (dest_MUX, data_MUX, alu_MUX, and_2_out);
  and and_1 (data_MUX, not_1_out, not_5_out, not_2_out, op_code[3]);
  and and_2 (and_2_out, op_code[0], op_code[1], op_code[2], not_3_out);
  and and_3 (alu_MUX, op_code[0], not_6_out, not_4_out, op_code[3]);
endmodule
